// Logisim project lab3Milestone1.circ as structural Verilog: 7 circuits, main circuit one_bit_adder
module main (
  input  [31:0] Instruction
);

  wire alu_ctrl_1_alu_src, clock_1_out;
  wire [3:0] alu_ctrl_1_alu_ctrl0;
  wire [31:0] alu32_1_r, bit_extender_1_out, multiplexer_1_out, register_file_1_rdata1,
       register_file_1_rdata2;

  Clock clock_1 (.out(clock_1_out));
  register_file register_file_1 (
    .RReg1(Instruction[19:15]), .RReg2(Instruction[24:20]), .WData(alu32_1_r), .Clock_in(clock_1_out),
    .Write(1'b1), .WReg(Instruction[11:7]), .RData1(register_file_1_rdata1), .RData2(register_file_1_rdata2));
  assign bit_extender_1_out = {{20{Instruction[31]}}, Instruction[31:20]};  // Bit_Extender bit_extender_1
  Multiplexer #(.enable("false"), .width(32)) multiplexer_1 (
    .in0(register_file_1_rdata2), .in1(bit_extender_1_out), .out(multiplexer_1_out), .sel(alu_ctrl_1_alu_src));
  ALU_Ctrl alu_ctrl_1 (
    .i30(Instruction[30]), .i14(Instruction[14]), .i13(Instruction[13]), .i12(Instruction[12]),
    .i6(Instruction[6]), .i5(Instruction[5]), .i4(Instruction[4]), .ALU_CTRL3(alu_ctrl_1_alu_ctrl0[3]),
    .ALU_CTRL2(alu_ctrl_1_alu_ctrl0[2]), .ALU_CTRL1(alu_ctrl_1_alu_ctrl0[1]),
    .ALU_CTRL0(alu_ctrl_1_alu_ctrl0[0]), .ALU_SRC(alu_ctrl_1_alu_src));
  ALU32 alu32_1 (
    .ALU_Ctrl(alu_ctrl_1_alu_ctrl0), .A(register_file_1_rdata1), .B(multiplexer_1_out), .R(alu32_1_r));  // open: C_out
endmodule

module one_bit_adder (
  input  A,
  input  B,
  input  Cin,
  output S,
  output Cout
);

  wire and_1_out, and_2_out, xor_1_out;

  xor xor_1 (xor_1_out, A, B);
  and and_1 (and_1_out, A, B);
  xor xor_2 (S, xor_1_out, Cin);
  and and_2 (and_2_out, xor_1_out, Cin);
  or or_1 (Cout, and_2_out, and_1_out);
endmodule

module one_bit_ALU (
  input  [3:0] ALU_Ctrl,
  input  A,
  input  B,
  input  C_in,
  output R,
  output C_out
);

  wire and_1_out, multiplexer_1_out, not_1_out, one_bit_adder_1_s, or_1_out, xor_1_out;

  not not_1 (not_1_out, B);
  Multiplexer #(.enable("false")) multiplexer_1 (.in0(B), .in1(not_1_out), .out(multiplexer_1_out), .sel(ALU_Ctrl[2]));
  and and_1 (and_1_out, A, multiplexer_1_out);
  or or_1 (or_1_out, A, multiplexer_1_out);
  xor xor_1 (xor_1_out, A, multiplexer_1_out);
  one_bit_adder one_bit_adder_1 (.A(A), .B(multiplexer_1_out), .Cin(C_in), .S(one_bit_adder_1_s), .Cout(C_out));
  Multiplexer #(.enable("false"), .select(2)) multiplexer_2 (
    .in0(and_1_out), .in1(or_1_out), .in2(xor_1_out), .in3(one_bit_adder_1_s), .out(R), .sel(ALU_Ctrl[1:0]));
endmodule

module ALU4 (
  input  [3:0] ALU_Ctrl,
  input  [3:0] A,
  input  [3:0] B,
  input  C_in,
  output [3:0] R,
  output C_out
);

  wire one_bit_alu_1_c_out, one_bit_alu_2_c_out, one_bit_alu_3_c_out;

  one_bit_ALU one_bit_alu_1 (
    .ALU_Ctrl(ALU_Ctrl), .A(A[0]), .B(B[0]), .C_in(C_in), .R(R[0]), .C_out(one_bit_alu_1_c_out));
  one_bit_ALU one_bit_alu_2 (
    .ALU_Ctrl(ALU_Ctrl), .A(A[1]), .B(B[1]), .C_in(one_bit_alu_1_c_out), .R(R[1]), .C_out(one_bit_alu_2_c_out));
  one_bit_ALU one_bit_alu_3 (
    .ALU_Ctrl(ALU_Ctrl), .A(A[2]), .B(B[2]), .C_in(one_bit_alu_2_c_out), .R(R[2]), .C_out(one_bit_alu_3_c_out));
  one_bit_ALU one_bit_alu_4 (
    .ALU_Ctrl(ALU_Ctrl), .A(A[3]), .B(B[3]), .C_in(one_bit_alu_3_c_out), .R(R[3]), .C_out(C_out));
endmodule

module ALU32 (
  input  [3:0] ALU_Ctrl,
  input  [31:0] A,
  input  [31:0] B,
  output [31:0] R,
  output C_out
);

  wire alu4_1_c_out, alu4_2_c_out, alu4_3_c_out, alu4_4_c_out, alu4_5_c_out, alu4_6_c_out, alu4_7_c_out;

  ALU4 alu4_1 (.ALU_Ctrl(ALU_Ctrl), .A(A[3:0]), .B(B[3:0]), .C_in(ALU_Ctrl[2]), .R(R[3:0]), .C_out(alu4_1_c_out));
  ALU4 alu4_2 (.ALU_Ctrl(ALU_Ctrl), .A(A[7:4]), .B(B[7:4]), .C_in(alu4_1_c_out), .R(R[7:4]), .C_out(alu4_2_c_out));
  ALU4 alu4_3 (.ALU_Ctrl(ALU_Ctrl), .A(A[11:8]), .B(B[11:8]), .C_in(alu4_2_c_out), .R(R[11:8]), .C_out(alu4_3_c_out));
  ALU4 alu4_4 (
    .ALU_Ctrl(ALU_Ctrl), .A(A[15:12]), .B(B[15:12]), .C_in(alu4_3_c_out), .R(R[15:12]), .C_out(alu4_4_c_out));
  ALU4 alu4_5 (
    .ALU_Ctrl(ALU_Ctrl), .A(A[19:16]), .B(B[19:16]), .C_in(alu4_4_c_out), .R(R[19:16]), .C_out(alu4_5_c_out));
  ALU4 alu4_6 (
    .ALU_Ctrl(ALU_Ctrl), .A(A[23:20]), .B(B[23:20]), .C_in(alu4_5_c_out), .R(R[23:20]), .C_out(alu4_6_c_out));
  ALU4 alu4_7 (
    .ALU_Ctrl(ALU_Ctrl), .A(A[27:24]), .B(B[27:24]), .C_in(alu4_6_c_out), .R(R[27:24]), .C_out(alu4_7_c_out));
  ALU4 alu4_8 (.ALU_Ctrl(ALU_Ctrl), .A(A[31:28]), .B(B[31:28]), .C_in(alu4_7_c_out), .R(R[31:28]), .C_out(C_out));
endmodule

module ALU_Ctrl (
  input  i30,
  input  i14,
  input  i13,
  input  i12,
  input  i6,
  input  i5,
  input  i4,
  output ALU_CTRL3,
  output ALU_CTRL2,
  output ALU_CTRL1,
  output ALU_CTRL0,
  output ALU_SRC
);

  wire and_2_out, not_1_out, not_2_out, not_3_out, not_4_out, not_5_out;

  not not_1 (not_1_out, i14);
  not not_2 (not_2_out, i13);
  not not_3 (not_3_out, i12);
  not not_4 (not_4_out, i5);
  not not_5 (not_5_out, i4);
  and and_1 (ALU_CTRL2, i30, not_2_out, i5);
  or or_1 (ALU_CTRL1, not_2_out, not_5_out);
  and and_2 (and_2_out, i13, not_3_out);
  or or_2 (ALU_SRC, not_4_out, not_5_out);
  or or_3 (ALU_CTRL0, not_1_out, and_2_out);

  assign ALU_CTRL3 = 1'b0;
endmodule

module register_file (
  input  [4:0] RReg1,
  input  [4:0] RReg2,
  input  [31:0] WData,
  input  Clock_in,
  input  Write,
  input  [4:0] WReg,
  output [31:0] RData1,
  output [31:0] RData2
);

  wire demultiplexer_1_out0, demultiplexer_1_out1, demultiplexer_1_out2, demultiplexer_1_out3,
       demultiplexer_1_out4, demultiplexer_1_out5, demultiplexer_1_out6, demultiplexer_1_out7,
       demultiplexer_1_out8, demultiplexer_1_out9, demultiplexer_1_out10, demultiplexer_1_out11,
       demultiplexer_1_out12, demultiplexer_1_out13, demultiplexer_1_out14, demultiplexer_1_out15,
       demultiplexer_1_out16, demultiplexer_1_out17, demultiplexer_1_out18, demultiplexer_1_out19,
       demultiplexer_1_out20, demultiplexer_1_out21, demultiplexer_1_out22, demultiplexer_1_out23,
       demultiplexer_1_out24, demultiplexer_1_out25, demultiplexer_1_out26, demultiplexer_1_out27,
       demultiplexer_1_out28, demultiplexer_1_out29, demultiplexer_1_out30, demultiplexer_1_out31;
  wire [31:0] Q0, Q1, Q2, Q3, Q4, Q5, Q6, Q7, Q8, Q9, Q10, Q11, Q12, Q13, Q14, Q15, Q16, Q17, Q18, Q19, Q20,
       Q21, Q22, Q23, Q24, Q25, Q26, Q27, Q28, Q29, Q30, Q31;

  Demultiplexer #(.enable("false"), .select(5)) demultiplexer_1 (
    .out0(demultiplexer_1_out0), .out1(demultiplexer_1_out1), .out2(demultiplexer_1_out2),
    .out3(demultiplexer_1_out3), .out4(demultiplexer_1_out4), .out5(demultiplexer_1_out5),
    .out6(demultiplexer_1_out6), .out7(demultiplexer_1_out7), .out8(demultiplexer_1_out8),
    .out9(demultiplexer_1_out9), .out10(demultiplexer_1_out10), .out11(demultiplexer_1_out11),
    .out12(demultiplexer_1_out12), .out13(demultiplexer_1_out13), .out14(demultiplexer_1_out14),
    .out15(demultiplexer_1_out15), .out16(demultiplexer_1_out16), .out17(demultiplexer_1_out17),
    .out18(demultiplexer_1_out18), .out19(demultiplexer_1_out19), .out20(demultiplexer_1_out20),
    .out21(demultiplexer_1_out21), .out22(demultiplexer_1_out22), .out23(demultiplexer_1_out23),
    .out24(demultiplexer_1_out24), .out25(demultiplexer_1_out25), .out26(demultiplexer_1_out26),
    .out27(demultiplexer_1_out27), .out28(demultiplexer_1_out28), .out29(demultiplexer_1_out29),
    .out30(demultiplexer_1_out30), .out31(demultiplexer_1_out31), .in(Write), .sel(WReg));
  Register #(.width(32)) register_1 (.D(WData), .en(demultiplexer_1_out0), .clk(Clock_in), .Q(Q0));  // open: clr
  Register #(.width(32)) register_2 (.D(WData), .en(demultiplexer_1_out1), .clk(Clock_in), .Q(Q1));  // open: clr
  Register #(.width(32)) register_3 (.D(WData), .en(demultiplexer_1_out2), .clk(Clock_in), .Q(Q2));  // open: clr
  Register #(.width(32)) register_4 (.D(WData), .en(demultiplexer_1_out3), .clk(Clock_in), .Q(Q3));  // open: clr
  Register #(.width(32)) register_5 (.D(WData), .en(demultiplexer_1_out4), .clk(Clock_in), .Q(Q4));  // open: clr
  Register #(.width(32)) register_6 (.D(WData), .en(demultiplexer_1_out5), .clk(Clock_in), .Q(Q5));  // open: clr
  Register #(.width(32)) register_7 (.D(WData), .en(demultiplexer_1_out6), .clk(Clock_in), .Q(Q6));  // open: clr
  Register #(.width(32)) register_8 (.D(WData), .en(demultiplexer_1_out7), .clk(Clock_in), .Q(Q7));  // open: clr
  Register #(.width(32)) register_9 (.D(WData), .en(demultiplexer_1_out8), .clk(Clock_in), .Q(Q8));  // open: clr
  Register #(.width(32)) register_10 (.D(WData), .en(demultiplexer_1_out9), .clk(Clock_in), .Q(Q9));  // open: clr
  Register #(.width(32)) register_11 (.D(WData), .en(demultiplexer_1_out10), .clk(Clock_in), .Q(Q10));  // open: clr
  Register #(.width(32)) register_12 (.D(WData), .en(demultiplexer_1_out11), .clk(Clock_in), .Q(Q11));  // open: clr
  Register #(.width(32)) register_13 (.D(WData), .en(demultiplexer_1_out12), .clk(Clock_in), .Q(Q12));  // open: clr
  Register #(.width(32)) register_14 (.D(WData), .en(demultiplexer_1_out13), .clk(Clock_in), .Q(Q13));  // open: clr
  Register #(.width(32)) register_15 (.D(WData), .en(demultiplexer_1_out14), .clk(Clock_in), .Q(Q14));  // open: clr
  Register #(.width(32)) register_16 (.D(WData), .en(demultiplexer_1_out15), .clk(Clock_in), .Q(Q15));  // open: clr
  Register #(.width(32)) register_17 (.D(WData), .en(demultiplexer_1_out16), .clk(Clock_in), .Q(Q16));  // open: clr
  Register #(.width(32)) register_18 (.D(WData), .en(demultiplexer_1_out17), .clk(Clock_in), .Q(Q17));  // open: clr
  Register #(.width(32)) register_19 (.D(WData), .en(demultiplexer_1_out18), .clk(Clock_in), .Q(Q18));  // open: clr
  Register #(.width(32)) register_20 (.D(WData), .en(demultiplexer_1_out19), .clk(Clock_in), .Q(Q19));  // open: clr
  Register #(.width(32)) register_21 (.D(WData), .en(demultiplexer_1_out20), .clk(Clock_in), .Q(Q20));  // open: clr
  Register #(.width(32)) register_22 (.D(WData), .en(demultiplexer_1_out21), .clk(Clock_in), .Q(Q21));  // open: clr
  Register #(.width(32)) register_23 (.D(WData), .en(demultiplexer_1_out22), .clk(Clock_in), .Q(Q22));  // open: clr
  Register #(.width(32)) register_24 (.D(WData), .en(demultiplexer_1_out23), .clk(Clock_in), .Q(Q23));  // open: clr
  Register #(.width(32)) register_25 (.D(WData), .en(demultiplexer_1_out24), .clk(Clock_in), .Q(Q24));  // open: clr
  Register #(.width(32)) register_26 (.D(WData), .en(demultiplexer_1_out25), .clk(Clock_in), .Q(Q25));  // open: clr
  Register #(.width(32)) register_27 (.D(WData), .en(demultiplexer_1_out26), .clk(Clock_in), .Q(Q26));  // open: clr
  Register #(.width(32)) register_28 (.D(WData), .en(demultiplexer_1_out27), .clk(Clock_in), .Q(Q27));  // open: clr
  Register #(.width(32)) register_29 (.D(WData), .en(demultiplexer_1_out28), .clk(Clock_in), .Q(Q28));  // open: clr
  Register #(.width(32)) register_30 (.D(WData), .en(demultiplexer_1_out29), .clk(Clock_in), .Q(Q29));  // open: clr
  Register #(.width(32)) register_31 (.D(WData), .en(demultiplexer_1_out30), .clk(Clock_in), .Q(Q30));  // open: clr
  Register #(.width(32)) register_32 (.D(WData), .en(demultiplexer_1_out31), .clk(Clock_in), .Q(Q31));  // open: clr
  Multiplexer #(.enable("false"), .select(5), .width(32)) multiplexer_1 (
    .in0(Q0), .in1(Q1), .in2(Q2), .in3(Q3), .in4(Q4), .in5(Q5), .in6(Q6), .in7(Q7), .in8(Q8), .in9(Q9),
    .in10(Q10), .in11(Q11), .in12(Q12), .in13(Q13), .in14(Q14), .in15(Q15), .in16(Q16), .in17(Q17),
    .in18(Q18), .in19(Q19), .in20(Q20), .in21(Q21), .in22(Q22), .in23(Q23), .in24(Q24), .in25(Q25),
    .in26(Q26), .in27(Q27), .in28(Q28), .in29(Q29), .in30(Q30), .in31(Q31), .out(RData1), .sel(RReg1));
  Multiplexer #(.enable("false"), .select(5), .width(32)) multiplexer_2 (
    .in0(Q0), .in1(Q1), .in2(Q2), .in3(Q3), .in4(Q4), .in5(Q5), .in6(Q6), .in7(Q7), .in8(Q8), .in9(Q9),
    .in10(Q10), .in11(Q11), .in12(Q12), .in13(Q13), .in14(Q14), .in15(Q15), .in16(Q16), .in17(Q17),
    .in18(Q18), .in19(Q19), .in20(Q20), .in21(Q21), .in22(Q22), .in23(Q23), .in24(Q24), .in25(Q25),
    .in26(Q26), .in27(Q27), .in28(Q28), .in29(Q29), .in30(Q30), .in31(Q31), .out(RData2), .sel(RReg2));
endmodule
